// Logisim project S1-T16.circ as structural Verilog: 9 circuits, main circuit main
module main (
  input  Rain,
  input  Wet_Soil,
  input  in_3,
  input  in_4,
  output [1:0] out_5
);

  wire and_1_out, bcd_to_7segment_1_s, bcd_to_7segment_1_u, bcd_to_7segment_1_v, bcd_to_7segment_1_w,
       bcd_to_7segment_1_x, bcd_to_7segment_1_y, bcd_to_7segment_1_z, bcd_to_7segment_2_s,
       bcd_to_7segment_2_u, bcd_to_7segment_2_v, bcd_to_7segment_2_w, bcd_to_7segment_2_x,
       bcd_to_7segment_2_y, bcd_to_7segment_2_z, bcd_to_7segment_3_s, bcd_to_7segment_3_u,
       bcd_to_7segment_3_v, bcd_to_7segment_3_w, bcd_to_7segment_3_x, bcd_to_7segment_3_y,
       bcd_to_7segment_3_z, bcd_to_7segment_4_s, bcd_to_7segment_4_u, bcd_to_7segment_4_v,
       bcd_to_7segment_4_w, bcd_to_7segment_4_x, bcd_to_7segment_4_y, bcd_to_7segment_4_z,
       bcd_to_7segment_5_s, bcd_to_7segment_5_u, bcd_to_7segment_5_v, bcd_to_7segment_5_w,
       bcd_to_7segment_5_x, bcd_to_7segment_5_y, bcd_to_7segment_5_z, bcd_to_7segment_6_s,
       bcd_to_7segment_6_u, bcd_to_7segment_6_v, bcd_to_7segment_6_w, bcd_to_7segment_6_x,
       bcd_to_7segment_6_y, bcd_to_7segment_6_z, bcd_to_7segment_7_s, bcd_to_7segment_7_u,
       bcd_to_7segment_7_v, bcd_to_7segment_7_w, bcd_to_7segment_7_x, bcd_to_7segment_7_y,
       bcd_to_7segment_7_z, bcd_to_7segment_8_s, bcd_to_7segment_8_u, bcd_to_7segment_8_v,
       bcd_to_7segment_8_w, bcd_to_7segment_8_x, bcd_to_7segment_8_y, bcd_to_7segment_8_z, button_1_out,
       clock_1_out, clock_2_out, comparator_1_eq, comparator_1_lt, d_ff_1_q, j_k_ff_1_q, n6bin_to_bcd_1_s,
       n6bin_to_bcd_1_t, n6bin_to_bcd_1_u, n6bin_to_bcd_1_v, n6bin_to_bcd_1_w, n6bin_to_bcd_1_x,
       n6bin_to_bcd_1_y, n6bin_to_bcd_1_z, n6bin_to_bcd_2_s, n6bin_to_bcd_2_t, n6bin_to_bcd_2_u,
       n6bin_to_bcd_2_v, n6bin_to_bcd_2_w, n6bin_to_bcd_2_x, n6bin_to_bcd_2_y, n6bin_to_bcd_2_z,
       n6bin_to_bcd_3_s, n6bin_to_bcd_3_t, n6bin_to_bcd_3_u, n6bin_to_bcd_3_v, n6bin_to_bcd_3_w,
       n6bin_to_bcd_3_x, n6bin_to_bcd_3_y, n6bin_to_bcd_3_z, n6bin_to_bcd_4_s, n6bin_to_bcd_4_t,
       n6bin_to_bcd_4_u, n6bin_to_bcd_4_v, n6bin_to_bcd_4_w, n6bin_to_bcd_4_x, n6bin_to_bcd_4_y,
       n6bin_to_bcd_4_z, nor_1_out, not_1_out, or_1_out, peak_check_lsb, peak_check_msb, peak_check_out_4,
       peak_check_out_5, peak_check_out_6, peak_check_peak, priority_sequencer_1_sequencer_active;
  wire [5:0] adder_1_out, multiplexer_1_out, quota_register_out_3, usage_register_out_5;

  Clock clock_1 (.out(clock_1_out));
  not not_1 (not_1_out, or_1_out);
  Clock clock_2 (.out(clock_2_out));
  priority_sequencer priority_sequencer_1 (
    .zone_is_watering(d_ff_1_q), .auto_cycle_start_btn(button_1_out), .clk(clock_1_out),
    .current_zone_select(out_5), .sequencer_active(priority_sequencer_1_sequencer_active));  // open: reset, out_6, start_pulse
  _6bin_to_bcd u_6bin_to_bcd_1 (
    .A(1'b0), .B(1'b0), .C(1'b0), .D(1'b0), .E(out_5[1]), .F(out_5[0]), .x(n6bin_to_bcd_1_x),
    .y(n6bin_to_bcd_1_y), .z(n6bin_to_bcd_1_z), .u(n6bin_to_bcd_1_u), .v(n6bin_to_bcd_1_v),
    .w(n6bin_to_bcd_1_w), .s(n6bin_to_bcd_1_s), .t(n6bin_to_bcd_1_t));
  peak_check peak_check (
    .enable(in_3), .clock(clock_2_out), .lsb(peak_check_lsb), .out_4(peak_check_out_4),
    .out_5(peak_check_out_5), .out_6(peak_check_out_6), .msb(peak_check_msb), .peak(peak_check_peak));
  bcd_to_7segment bcd_to_7segment_1 (
    .a(n6bin_to_bcd_1_x), .b(n6bin_to_bcd_1_y), .c(n6bin_to_bcd_1_z), .d(n6bin_to_bcd_1_u),
    .x(bcd_to_7segment_1_x), .y(bcd_to_7segment_1_y), .z(bcd_to_7segment_1_z), .u(bcd_to_7segment_1_u),
    .v(bcd_to_7segment_1_v), .w(bcd_to_7segment_1_w), .s(bcd_to_7segment_1_s));
  bcd_to_7segment bcd_to_7segment_2 (
    .a(n6bin_to_bcd_1_v), .b(n6bin_to_bcd_1_w), .c(n6bin_to_bcd_1_s), .d(n6bin_to_bcd_1_t),
    .x(bcd_to_7segment_2_x), .y(bcd_to_7segment_2_y), .z(bcd_to_7segment_2_z), .u(bcd_to_7segment_2_u),
    .v(bcd_to_7segment_2_v), .w(bcd_to_7segment_2_w), .s(bcd_to_7segment_2_s));
  quota_register quota_register (.clk(clock_1_out), .user(out_5), .out_3(quota_register_out_3));
  usage_register usage_register (
    .usage(adder_1_out), .reset(not_1_out), .user(out_5), .save(j_k_ff_1_q), .out_5(usage_register_out_5));
  nor nor_1 (nor_1_out, Wet_Soil, Rain, in_4);
  Multiplexer #(.width(6)) multiplexer_1 (
    .in0(6'b000001), .in1(6'b000010), .out(multiplexer_1_out), .sel(peak_check_peak));  // open: en
  Adder #(.width(6)) adder_1 (.a(usage_register_out_5), .b(multiplexer_1_out), .out(adder_1_out));  // open: cin, cout
  _7_Segment_Display u_7_segment_display_1 (
    .g(bcd_to_7segment_1_s), .f(bcd_to_7segment_1_w), .a(bcd_to_7segment_1_x), .b(bcd_to_7segment_1_y),
    .e(bcd_to_7segment_1_v), .d(bcd_to_7segment_1_u), .c(bcd_to_7segment_1_z));  // open: dp
  _7_Segment_Display u_7_segment_display_2 (
    .g(bcd_to_7segment_2_s), .f(bcd_to_7segment_2_w), .a(bcd_to_7segment_2_x), .b(bcd_to_7segment_2_y),
    .e(bcd_to_7segment_2_v), .d(bcd_to_7segment_2_u), .c(bcd_to_7segment_2_z));  // open: dp
  Comparator #(.width(6)) comparator_1 (
    .a(adder_1_out), .b(quota_register_out_3), .eq(comparator_1_eq), .lt(comparator_1_lt));  // open: gt
  or or_1 (or_1_out, comparator_1_eq, comparator_1_lt);
  _6bin_to_bcd u_6bin_to_bcd_2 (
    .A(1'b0), .B(peak_check_msb), .C(peak_check_out_6), .D(peak_check_out_5), .E(peak_check_out_4),
    .F(peak_check_lsb), .x(n6bin_to_bcd_2_x), .y(n6bin_to_bcd_2_y), .z(n6bin_to_bcd_2_z),
    .u(n6bin_to_bcd_2_u), .v(n6bin_to_bcd_2_v), .w(n6bin_to_bcd_2_w), .s(n6bin_to_bcd_2_s),
    .t(n6bin_to_bcd_2_t));
  and and_1 (and_1_out, or_1_out, priority_sequencer_1_sequencer_active, nor_1_out);
  bcd_to_7segment bcd_to_7segment_3 (
    .a(n6bin_to_bcd_2_v), .b(n6bin_to_bcd_2_w), .c(n6bin_to_bcd_2_s), .d(n6bin_to_bcd_2_t),
    .x(bcd_to_7segment_3_x), .y(bcd_to_7segment_3_y), .z(bcd_to_7segment_3_z), .u(bcd_to_7segment_3_u),
    .v(bcd_to_7segment_3_v), .w(bcd_to_7segment_3_w), .s(bcd_to_7segment_3_s));
  J_K_Flip_Flop j_k_ff_1 (
    .J(and_1_out), .clk(clock_1_out), .K(and_1_out), .Q(j_k_ff_1_q));  // open: Qn, preset, en, reset
  D_Flip_Flop d_ff_1 (.clk(clock_1_out), .D(or_1_out), .Q(d_ff_1_q));  // open: Qn, preset, en, reset
  bcd_to_7segment bcd_to_7segment_4 (
    .a(n6bin_to_bcd_2_x), .b(n6bin_to_bcd_2_y), .c(n6bin_to_bcd_2_z), .d(n6bin_to_bcd_2_u),
    .x(bcd_to_7segment_4_x), .y(bcd_to_7segment_4_y), .z(bcd_to_7segment_4_z), .u(bcd_to_7segment_4_u),
    .v(bcd_to_7segment_4_v), .w(bcd_to_7segment_4_w), .s(bcd_to_7segment_4_s));
  _7_Segment_Display u_7_segment_display_3 (
    .g(bcd_to_7segment_4_s), .f(bcd_to_7segment_4_w), .a(bcd_to_7segment_4_x), .b(bcd_to_7segment_4_y),
    .e(bcd_to_7segment_4_v), .d(bcd_to_7segment_4_u), .c(bcd_to_7segment_4_z));  // open: dp
  _7_Segment_Display u_7_segment_display_4 (
    .g(bcd_to_7segment_3_s), .f(bcd_to_7segment_3_w), .a(bcd_to_7segment_3_x), .b(bcd_to_7segment_3_y),
    .e(bcd_to_7segment_3_v), .d(bcd_to_7segment_3_u), .c(bcd_to_7segment_3_z));  // open: dp
  _6bin_to_bcd u_6bin_to_bcd_3 (
    .A(quota_register_out_3[5]), .B(quota_register_out_3[4]), .C(quota_register_out_3[3]),
    .D(quota_register_out_3[2]), .E(quota_register_out_3[1]), .F(quota_register_out_3[0]),
    .x(n6bin_to_bcd_3_x), .y(n6bin_to_bcd_3_y), .z(n6bin_to_bcd_3_z), .u(n6bin_to_bcd_3_u),
    .v(n6bin_to_bcd_3_v), .w(n6bin_to_bcd_3_w), .s(n6bin_to_bcd_3_s), .t(n6bin_to_bcd_3_t));
  bcd_to_7segment bcd_to_7segment_5 (
    .a(n6bin_to_bcd_3_x), .b(n6bin_to_bcd_3_y), .c(n6bin_to_bcd_3_z), .d(n6bin_to_bcd_3_u),
    .x(bcd_to_7segment_5_x), .y(bcd_to_7segment_5_y), .z(bcd_to_7segment_5_z), .u(bcd_to_7segment_5_u),
    .v(bcd_to_7segment_5_v), .w(bcd_to_7segment_5_w), .s(bcd_to_7segment_5_s));
  bcd_to_7segment bcd_to_7segment_6 (
    .a(n6bin_to_bcd_3_v), .b(n6bin_to_bcd_3_w), .c(n6bin_to_bcd_3_s), .d(n6bin_to_bcd_3_t),
    .x(bcd_to_7segment_6_x), .y(bcd_to_7segment_6_y), .z(bcd_to_7segment_6_z), .u(bcd_to_7segment_6_u),
    .v(bcd_to_7segment_6_v), .w(bcd_to_7segment_6_w), .s(bcd_to_7segment_6_s));
  _6bin_to_bcd u_6bin_to_bcd_4 (
    .A(usage_register_out_5[5]), .B(usage_register_out_5[4]), .C(usage_register_out_5[3]),
    .D(usage_register_out_5[2]), .E(usage_register_out_5[1]), .F(usage_register_out_5[0]),
    .x(n6bin_to_bcd_4_x), .y(n6bin_to_bcd_4_y), .z(n6bin_to_bcd_4_z), .u(n6bin_to_bcd_4_u),
    .v(n6bin_to_bcd_4_v), .w(n6bin_to_bcd_4_w), .s(n6bin_to_bcd_4_s), .t(n6bin_to_bcd_4_t));
  _7_Segment_Display u_7_segment_display_5 (
    .g(bcd_to_7segment_5_s), .f(bcd_to_7segment_5_w), .a(bcd_to_7segment_5_x), .b(bcd_to_7segment_5_y),
    .e(bcd_to_7segment_5_v), .d(bcd_to_7segment_5_u), .c(bcd_to_7segment_5_z));  // open: dp
  bcd_to_7segment bcd_to_7segment_7 (
    .a(n6bin_to_bcd_4_v), .b(n6bin_to_bcd_4_w), .c(n6bin_to_bcd_4_s), .d(n6bin_to_bcd_4_t),
    .x(bcd_to_7segment_7_x), .y(bcd_to_7segment_7_y), .z(bcd_to_7segment_7_z), .u(bcd_to_7segment_7_u),
    .v(bcd_to_7segment_7_v), .w(bcd_to_7segment_7_w), .s(bcd_to_7segment_7_s));
  _7_Segment_Display u_7_segment_display_6 (
    .g(bcd_to_7segment_6_s), .f(bcd_to_7segment_6_w), .a(bcd_to_7segment_6_x), .b(bcd_to_7segment_6_y),
    .e(bcd_to_7segment_6_v), .d(bcd_to_7segment_6_u), .c(bcd_to_7segment_6_z));  // open: dp
  bcd_to_7segment bcd_to_7segment_8 (
    .a(n6bin_to_bcd_4_x), .b(n6bin_to_bcd_4_y), .c(n6bin_to_bcd_4_z), .d(n6bin_to_bcd_4_u),
    .x(bcd_to_7segment_8_x), .y(bcd_to_7segment_8_y), .z(bcd_to_7segment_8_z), .u(bcd_to_7segment_8_u),
    .v(bcd_to_7segment_8_v), .w(bcd_to_7segment_8_w), .s(bcd_to_7segment_8_s));
  Button button_1 (.out(button_1_out));
  _7_Segment_Display u_7_segment_display_7 (
    .g(bcd_to_7segment_8_s), .f(bcd_to_7segment_8_w), .a(bcd_to_7segment_8_x), .b(bcd_to_7segment_8_y),
    .e(bcd_to_7segment_8_v), .d(bcd_to_7segment_8_u), .c(bcd_to_7segment_8_z));  // open: dp
  _7_Segment_Display u_7_segment_display_8 (
    .g(bcd_to_7segment_7_s), .f(bcd_to_7segment_7_w), .a(bcd_to_7segment_7_x), .b(bcd_to_7segment_7_y),
    .e(bcd_to_7segment_7_v), .d(bcd_to_7segment_7_u), .c(bcd_to_7segment_7_z));  // open: dp
  LED led_1 (.in(priority_sequencer_1_sequencer_active));

  // Notes on the sheet:
  //   ZONE SELECT
  //   24 HR CLOCK
  //   AUTOMATIC SEQUENCE START 
  //   ZONE QUOTA
  //   ZONE USAGE
  //   SEQUENCE ACTIVE INDICATOR
  //   PAUSE OPERATION
endmodule

module _6bin_to_bcd (
  input  A,
  input  B,
  input  C,
  input  D,
  input  E,
  input  F,
  output x,
  output y,
  output z,
  output u,
  output v,
  output w,
  output s,
  output t
);

  wire and_1_out, and_2_out, and_3_out, and_4_out, and_5_out, and_6_out, and_7_out, and_8_out, and_9_out,
       and_10_out, and_11_out, and_12_out, and_13_out, and_14_out, and_15_out, and_16_out, and_17_out,
       and_18_out, and_19_out, and_20_out, and_21_out, and_22_out, and_23_out, and_24_out, and_25_out,
       and_26_out, and_27_out, and_28_out, and_29_out, and_30_out, and_31_out, and_32_out, and_33_out,
       and_34_out, and_35_out, and_36_out, and_37_out, and_38_out, not_1_out, not_2_out, not_3_out,
       not_4_out, not_5_out, not_6_out, not_7_out, not_8_out, not_9_out, not_10_out, not_11_out, not_12_out,
       not_13_out, not_14_out, not_15_out, not_16_out, not_17_out, not_18_out, not_19_out, not_20_out,
       not_21_out, not_22_out, not_23_out, not_24_out, not_25_out, not_26_out, not_27_out, not_28_out,
       not_29_out, not_30_out, not_31_out, not_32_out, not_33_out, not_34_out, not_35_out, not_36_out,
       not_37_out, not_38_out, not_39_out, not_40_out, not_41_out, not_42_out, not_43_out, not_44_out,
       not_45_out, not_46_out, not_47_out, not_48_out, not_49_out, not_50_out, not_51_out, not_52_out,
       not_53_out, not_54_out, not_55_out, not_56_out, not_57_out, not_58_out, not_59_out, not_60_out,
       not_61_out, not_62_out, not_63_out, not_64_out, not_65_out, not_66_out, not_67_out, not_68_out,
       not_69_out, not_70_out, not_71_out;

  and and_1 (and_1_out, A, C);
  and and_2 (and_2_out, A, B);
  not not_1 (not_1_out, A);
  not not_2 (not_2_out, A);
  not not_3 (not_3_out, B);
  not not_4 (not_4_out, C);
  not not_5 (not_5_out, A);
  not not_6 (not_6_out, B);
  not not_7 (not_7_out, A);
  not not_8 (not_8_out, B);
  not not_9 (not_9_out, A);
  not not_10 (not_10_out, A);
  not not_11 (not_11_out, C);
  not not_12 (not_12_out, D);
  not not_13 (not_13_out, B);
  not not_14 (not_14_out, C);
  not not_15 (not_15_out, C);
  not not_16 (not_16_out, C);
  not not_17 (not_17_out, D);
  not not_18 (not_18_out, A);
  not not_19 (not_19_out, B);
  not not_20 (not_20_out, D);
  not not_21 (not_21_out, E);
  not not_22 (not_22_out, A);
  not not_23 (not_23_out, C);
  not not_24 (not_24_out, D);
  not not_25 (not_25_out, A);
  not not_26 (not_26_out, E);
  not not_27 (not_27_out, B);
  not not_28 (not_28_out, C);
  not not_29 (not_29_out, C);
  not not_30 (not_30_out, D);
  not not_31 (not_31_out, E);
  not not_32 (not_32_out, D);
  not not_33 (not_33_out, B);
  not not_34 (not_34_out, C);
  not not_35 (not_35_out, E);
  not not_36 (not_36_out, A);
  not not_37 (not_37_out, B);
  not not_38 (not_38_out, A);
  not not_39 (not_39_out, D);
  not not_40 (not_40_out, E);
  not not_41 (not_41_out, A);
  not not_42 (not_42_out, D);
  not not_43 (not_43_out, D);
  not not_44 (not_44_out, E);
  not not_45 (not_45_out, B);
  not not_46 (not_46_out, C);
  not not_47 (not_47_out, D);
  not not_48 (not_48_out, B);
  not not_49 (not_49_out, C);
  not not_50 (not_50_out, A);
  not not_51 (not_51_out, B);
  not not_52 (not_52_out, C);
  not not_53 (not_53_out, A);
  not not_54 (not_54_out, C);
  not not_55 (not_55_out, A);
  not not_56 (not_56_out, B);
  not not_57 (not_57_out, E);
  not not_58 (not_58_out, A);
  not not_59 (not_59_out, C);
  not not_60 (not_60_out, D);
  not not_61 (not_61_out, E);
  not not_62 (not_62_out, A);
  not not_63 (not_63_out, D);
  not not_64 (not_64_out, B);
  not not_65 (not_65_out, C);
  not not_66 (not_66_out, E);
  not not_67 (not_67_out, C);
  not not_68 (not_68_out, E);
  not not_69 (not_69_out, B);
  not not_70 (not_70_out, D);
  not not_71 (not_71_out, E);
  or or_1 (y, and_1_out, and_2_out);
  and and_3 (and_3_out, not_1_out, B, D);
  and and_4 (and_4_out, not_2_out, B, C);
  and and_5 (and_5_out, B, C, D);
  and and_6 (and_6_out, A, not_3_out, not_4_out);
  and and_7 (and_7_out, not_5_out, not_6_out, C, E);
  and and_8 (and_8_out, not_7_out, not_8_out, C, D);
  and and_9 (and_9_out, not_9_out, C, D, E);
  and and_10 (and_10_out, not_10_out, B, not_11_out, not_12_out);
  and and_11 (and_11_out, A, not_13_out, not_14_out);
  and and_12 (and_12_out, A, not_15_out, E);
  and and_13 (and_13_out, A, not_16_out, D);
  and and_14 (and_14_out, A, B, C, not_17_out);
  and and_15 (and_15_out, not_18_out, not_19_out, C, not_20_out, not_21_out);
  and and_16 (and_16_out, not_22_out, B, not_23_out, not_24_out, E);
  and and_17 (and_17_out, not_25_out, B, C, D, not_26_out);
  and and_18 (and_18_out, A, not_27_out, not_28_out, D, E);
  and and_19 (and_19_out, A, B, not_29_out, not_30_out, not_31_out);
  and and_20 (and_20_out, A, B, C, not_32_out, E);
  and and_21 (and_21_out, not_33_out, not_34_out, D, not_35_out);
  and and_22 (and_22_out, not_36_out, not_37_out, D, E);
  and and_23 (and_23_out, not_38_out, B, not_39_out, not_40_out);
  and and_24 (and_24_out, not_41_out, B, C, not_42_out);
  and and_25 (and_25_out, B, C, not_43_out, not_44_out);
  and and_26 (and_26_out, A, not_45_out, not_46_out, not_47_out, E);
  and and_27 (and_27_out, A, not_48_out, C, D);
  and and_28 (and_28_out, A, B, not_49_out, D, E);
  and and_29 (and_29_out, not_50_out, not_51_out, not_52_out, E);
  and and_30 (and_30_out, not_53_out, not_54_out, D, E);
  and and_31 (and_31_out, not_55_out, not_56_out, C, D, not_57_out);
  and and_32 (and_32_out, not_58_out, B, not_59_out, not_60_out, not_61_out);
  and and_33 (and_33_out, not_62_out, B, C, not_63_out, E);
  and and_34 (and_34_out, A, not_64_out, not_65_out, not_66_out);
  and and_35 (and_35_out, A, not_67_out, D, not_68_out);
  and and_36 (and_36_out, A, not_69_out, C, E);
  and and_37 (and_37_out, A, C, D, E);
  and and_38 (and_38_out, A, B, C, not_70_out, not_71_out);
  or or_2 (z, and_3_out, and_4_out, and_5_out, and_6_out);
  or or_3 (u, and_7_out, and_8_out, and_9_out, and_10_out, and_11_out, and_12_out, and_13_out, and_14_out);
  or or_4 (v, and_15_out, and_16_out, and_17_out, and_18_out, and_19_out, and_20_out);
  or or_5 (w, and_21_out, and_22_out, and_23_out, and_24_out, and_25_out, and_26_out, and_27_out, and_28_out);
  or or_6 (s, and_29_out, and_30_out, and_31_out, and_32_out, and_33_out, and_34_out, and_35_out, and_36_out, and_37_out, and_38_out);

  assign t = F;
  assign x = 1'b0;
endmodule

module bcd_to_7segment (
  input  a,
  input  b,
  input  c,
  input  d,
  output x,
  output y,
  output z,
  output u,
  output v,
  output w,
  output s
);

  wire and_1_out, and_2_out, and_3_out, and_4_out, and_5_out, and_6_out, and_7_out, and_8_out, and_9_out,
       and_10_out, and_11_out, and_12_out, and_13_out, and_14_out, and_15_out, and_16_out, and_17_out,
       and_18_out, and_19_out, and_20_out, and_21_out, and_22_out, and_23_out, and_24_out, and_25_out,
       and_26_out, not_1_out, not_2_out, not_3_out, not_4_out, not_5_out, not_6_out, not_7_out, not_8_out,
       not_9_out, not_10_out, not_11_out, not_12_out, not_13_out, not_14_out, not_15_out, not_16_out,
       not_17_out, not_18_out, not_19_out, not_20_out, not_21_out, not_22_out, not_23_out, not_24_out,
       not_25_out, not_26_out, not_27_out, not_28_out, not_29_out, not_30_out, not_31_out, not_32_out,
       not_33_out, not_34_out, not_35_out, not_36_out, not_37_out, not_38_out, not_39_out, not_40_out,
       not_41_out, not_42_out, not_43_out, not_44_out, not_45_out, not_46_out, not_47_out, not_48_out,
       not_49_out, not_50_out, not_51_out, not_52_out;

  and and_1 (and_1_out, c, not_1_out);
  not not_1 (not_1_out, a);
  and and_2 (and_2_out, b, d, not_2_out);
  not not_2 (not_2_out, a);
  and and_3 (and_3_out, a, not_3_out, not_4_out);
  not not_3 (not_3_out, b);
  not not_4 (not_4_out, c);
  not not_5 (not_5_out, a);
  not not_6 (not_6_out, b);
  and and_4 (and_4_out, not_5_out, not_6_out, not_7_out);
  not not_7 (not_7_out, d);
  not not_8 (not_8_out, a);
  and and_5 (and_5_out, not_8_out, not_9_out);
  not not_9 (not_9_out, b);
  not not_10 (not_10_out, b);
  and and_6 (and_6_out, not_10_out, not_11_out);
  not not_11 (not_11_out, c);
  and and_7 (and_7_out, c, d, not_12_out);
  not not_12 (not_12_out, a);
  not not_13 (not_13_out, a);
  and and_8 (and_8_out, not_13_out, not_14_out, not_15_out);
  not not_14 (not_14_out, c);
  not not_15 (not_15_out, d);
  and and_9 (and_9_out, b, not_16_out);
  not not_16 (not_16_out, a);
  and and_10 (and_10_out, d, not_17_out);
  not not_17 (not_17_out, a);
  not not_18 (not_18_out, b);
  and and_11 (and_11_out, not_18_out, not_19_out);
  not not_19 (not_19_out, c);
  not not_20 (not_20_out, b);
  not not_21 (not_21_out, c);
  not not_22 (not_22_out, a);
  not not_23 (not_23_out, b);
  not not_24 (not_24_out, a);
  not not_25 (not_25_out, d);
  not not_26 (not_26_out, a);
  not not_27 (not_27_out, b);
  not not_28 (not_28_out, d);
  not not_29 (not_29_out, a);
  not not_30 (not_30_out, c);
  not not_31 (not_31_out, a);
  and and_12 (and_12_out, c, not_31_out, not_32_out);
  not not_32 (not_32_out, d);
  not not_33 (not_33_out, b);
  and and_13 (and_13_out, not_33_out, not_34_out, not_35_out);
  not not_34 (not_34_out, c);
  not not_35 (not_35_out, d);
  not not_36 (not_36_out, b);
  and and_14 (and_14_out, a, not_36_out, not_37_out);
  not not_37 (not_37_out, c);
  and and_15 (and_15_out, b, not_38_out, not_39_out);
  not not_38 (not_38_out, a);
  not not_39 (not_39_out, c);
  and and_16 (and_16_out, b, not_40_out, not_41_out);
  not not_40 (not_40_out, a);
  not not_41 (not_41_out, d);
  not not_42 (not_42_out, a);
  and and_17 (and_17_out, not_42_out, not_43_out, not_44_out);
  not not_43 (not_43_out, c);
  not not_44 (not_44_out, d);
  not not_45 (not_45_out, b);
  and and_18 (and_18_out, a, not_45_out, not_46_out);
  not not_46 (not_46_out, c);
  and and_19 (and_19_out, b, not_47_out, not_48_out);
  not not_47 (not_47_out, a);
  not not_48 (not_48_out, c);
  not not_49 (not_49_out, a);
  and and_20 (and_20_out, c, not_49_out, not_50_out);
  not not_50 (not_50_out, b);
  not not_51 (not_51_out, a);
  and and_21 (and_21_out, c, not_51_out, not_52_out);
  not not_52 (not_52_out, d);
  or or_1 (x, and_1_out, and_2_out, and_3_out, and_4_out);
  or or_2 (y, and_5_out, and_6_out, and_7_out, and_8_out);
  or or_3 (z, and_9_out, and_10_out, and_11_out);
  and and_22 (and_22_out, a, not_20_out, not_21_out);
  and and_23 (and_23_out, c, not_22_out, not_23_out);
  and and_24 (and_24_out, c, not_24_out, not_25_out);
  and and_25 (and_25_out, not_26_out, not_27_out, not_28_out);
  and and_26 (and_26_out, b, d, not_29_out, not_30_out);
  or or_4 (v, and_12_out, and_13_out);
  or or_5 (w, and_14_out, and_15_out, and_16_out, and_17_out);
  or or_6 (s, and_18_out, and_19_out, and_20_out, and_21_out);
  or or_7 (u, and_22_out, and_23_out, and_24_out, and_25_out, and_26_out);
endmodule

module priority_sequencer (
  input  zone_is_watering,
  input  auto_cycle_start_btn,
  input  clk,
  input  reset,
  output [1:0] current_zone_select,
  output [2:0] out_6,
  output start_pulse,
  output sequencer_active
);

  wire d_ff_1_q, not_1_out, zone_finished_pulse_out;
  wire [2:0] multiplexer_1_out, multiplexer_2_out, multiplexer_3_out, multiplexer_4_out, multiplexer_5_out,
       multiplexer_6_out;

  Register #(.width(3)) register_1 (.D(multiplexer_6_out), .Q(out_6), .clk(clk), .clr(reset));  // open: en
  D_Flip_Flop d_ff_1 (.clk(clk), .D(zone_is_watering), .Q(d_ff_1_q), .reset(reset));  // open: Qn, preset, en
  not not_1 (not_1_out, zone_is_watering);
  and zone_finished_pulse (zone_finished_pulse_out, d_ff_1_q, not_1_out);
  Multiplexer #(.width(3)) multiplexer_1 (
    .in0(3'b000), .in1(3'b001), .out(multiplexer_1_out), .sel(auto_cycle_start_btn));  // open: en
  Multiplexer #(.width(3)) multiplexer_2 (
    .in0(3'b001), .in1(3'b010), .out(multiplexer_2_out), .sel(zone_finished_pulse_out));  // open: en
  Multiplexer #(.width(3)) multiplexer_3 (
    .in0(3'b010), .in1(3'b011), .out(multiplexer_3_out), .sel(zone_finished_pulse_out));  // open: en
  Multiplexer #(.width(3)) multiplexer_4 (
    .in0(3'b011), .in1(3'b100), .out(multiplexer_4_out), .sel(zone_finished_pulse_out));  // open: en
  Multiplexer #(.width(3)) multiplexer_5 (
    .in0(3'b100), .in1(3'b000), .out(multiplexer_5_out), .sel(zone_finished_pulse_out));  // open: en
  Multiplexer #(.select(3), .width(3)) multiplexer_6 (
    .in0(multiplexer_1_out), .in1(multiplexer_2_out), .in2(multiplexer_3_out), .in3(multiplexer_4_out),
    .in4(multiplexer_5_out), .in5(3'b000), .in6(3'b000), .in7(3'b000), .out(multiplexer_6_out), .sel(out_6));  // open: en
  Multiplexer #(.select(3), .width(2)) multiplexer_7 (
    .in0(2'b00), .in1(2'b10), .in2(2'b00), .in3(2'b11), .in4(2'b01), .in5(2'b00), .in6(2'b00), .in7(2'b00),
    .out(current_zone_select), .sel(out_6));  // open: en
  or or_1 (sequencer_active, out_6[0], out_6[1], out_6[2]);
  Multiplexer #(.select(3)) multiplexer_8 (
    .in0(auto_cycle_start_btn), .in1(zone_finished_pulse_out), .in2(zone_finished_pulse_out),
    .in3(zone_finished_pulse_out), .in4(zone_finished_pulse_out), .in5(1'b0), .in6(1'b0), .in7(1'b0),
    .out(start_pulse), .sel(out_6));  // open: en
endmodule

module usage_register (
  input  [5:0] usage,
  input  reset,
  input  [1:0] user,
  input  save,
  output [5:0] out_5
);

  wire demultiplexer_1_out0, demultiplexer_1_out1, demultiplexer_1_out2, demultiplexer_1_out3, or_1_out;
  wire [5:0] multiplexer_1_out, register_1_q, register_2_q, register_3_q, register_4_q;

  Multiplexer #(.width(6)) multiplexer_1 (
    .in0(usage), .in1({6{1'b0}}), .out(multiplexer_1_out), .sel(reset));  // open: en
  Register #(.width(6)) register_1 (
    .D(multiplexer_1_out), .Q(register_1_q), .clk(demultiplexer_1_out0));  // open: en, clr
  Register #(.width(6)) register_2 (
    .D(multiplexer_1_out), .Q(register_2_q), .clk(demultiplexer_1_out1));  // open: en, clr
  Register #(.width(6)) register_3 (
    .D(multiplexer_1_out), .Q(register_3_q), .clk(demultiplexer_1_out2));  // open: en, clr
  Register #(.width(6)) register_4 (
    .D(multiplexer_1_out), .Q(register_4_q), .clk(demultiplexer_1_out3));  // open: en, clr
  or or_1 (or_1_out, reset, save);
  Demultiplexer #(.select(2)) demultiplexer_1 (
    .out0(demultiplexer_1_out0), .out1(demultiplexer_1_out1), .out2(demultiplexer_1_out2),
    .out3(demultiplexer_1_out3), .in(or_1_out), .sel(user));  // open: en
  Multiplexer #(.select(2), .width(6)) multiplexer_2 (
    .in0(register_1_q), .in1(register_2_q), .in2(register_3_q), .in3(register_4_q), .out(out_5), .sel(user));  // open: en
endmodule

module quota_register (
  input  clk,
  input  [1:0] user,
  output [5:0] out_3
);

  wire demultiplexer_1_out0, demultiplexer_1_out1, demultiplexer_1_out2, demultiplexer_1_out3;
  wire [5:0] register_1_q, register_2_q, register_3_q, register_4_q;

  Demultiplexer #(.select(2)) demultiplexer_1 (
    .out0(demultiplexer_1_out0), .out1(demultiplexer_1_out1), .out2(demultiplexer_1_out2),
    .out3(demultiplexer_1_out3), .in(clk), .sel(user));  // open: en
  Register #(.width(6)) register_1 (.D(6'b001111), .Q(register_1_q), .clk(demultiplexer_1_out0));  // open: en, clr
  Register #(.width(6)) register_2 (.D(6'b001101), .Q(register_2_q), .clk(demultiplexer_1_out1));  // open: en, clr
  Register #(.width(6)) register_3 (.D(6'b010100), .Q(register_3_q), .clk(demultiplexer_1_out2));  // open: en, clr
  Register #(.width(6)) register_4 (.D(6'b001111), .Q(register_4_q), .clk(demultiplexer_1_out3));  // open: en, clr
  Multiplexer #(.select(2), .width(6)) multiplexer_1 (
    .in0(register_1_q), .in1(register_2_q), .in2(register_3_q), .in3(register_4_q), .out(out_3), .sel(user));  // open: en
endmodule

module peak_check (
  input  enable,
  input  clock,
  output lsb,
  output out_4,
  output out_5,
  output out_6,
  output msb,
  output peak
);

  wire comparator_1_gt, comparator_2_lt;

  clock_counter clock_counter_1 (
    .in_1(enable), .clk(clock), .lsb(lsb), .out_4(out_4), .out_5(out_5), .out_6(out_6), .msb(msb));
  Comparator #(.width(5), .mode("unsigned")) comparator_1 (
    .a({msb, out_6, out_5, out_4, lsb}), .b(5'b01001), .gt(comparator_1_gt));  // open: eq, lt
  Comparator #(.width(5), .mode("unsigned")) comparator_2 (
    .a({msb, out_6, out_5, out_4, lsb}), .b(5'b10001), .lt(comparator_2_lt));  // open: gt, eq
  and and_1 (peak, comparator_1_gt, comparator_2_lt);
endmodule

module clock_counter (
  input  in_1,
  input  clk,
  output lsb,
  output out_4,
  output out_5,
  output out_6,
  output msb
);

  wire and_1_out, j_k_ff_1_qn, j_k_ff_2_qn, j_k_ff_3_qn, j_k_ff_4_qn;

  J_K_Flip_Flop j_k_ff_1 (
    .J(in_1), .clk(clk), .K(in_1), .Q(lsb), .Qn(j_k_ff_1_qn), .reset(and_1_out));  // open: preset, en
  J_K_Flip_Flop j_k_ff_2 (
    .J(in_1), .clk(j_k_ff_1_qn), .K(in_1), .Q(out_4), .Qn(j_k_ff_2_qn), .reset(and_1_out));  // open: preset, en
  J_K_Flip_Flop j_k_ff_3 (
    .J(in_1), .clk(j_k_ff_2_qn), .K(in_1), .Q(out_5), .Qn(j_k_ff_3_qn), .reset(and_1_out));  // open: preset, en
  J_K_Flip_Flop j_k_ff_4 (
    .J(in_1), .clk(j_k_ff_3_qn), .K(in_1), .Q(out_6), .Qn(j_k_ff_4_qn), .reset(and_1_out));  // open: preset, en
  J_K_Flip_Flop j_k_ff_5 (.J(in_1), .clk(j_k_ff_4_qn), .K(in_1), .Q(msb), .reset(and_1_out));  // open: Qn, preset, en
  and and_1 (and_1_out, j_k_ff_1_qn, j_k_ff_3_qn, j_k_ff_2_qn, out_6, msb);
endmodule

module display_template (
  input  in_1,
  input  in_2,
  input  in_3,
  input  in_4,
  input  in_5,
  input  in_6
);

  wire bcd_to_7segment_1_s, bcd_to_7segment_1_u, bcd_to_7segment_1_v, bcd_to_7segment_1_w,
       bcd_to_7segment_1_x, bcd_to_7segment_1_y, bcd_to_7segment_1_z, bcd_to_7segment_2_s,
       bcd_to_7segment_2_u, bcd_to_7segment_2_v, bcd_to_7segment_2_w, bcd_to_7segment_2_x,
       bcd_to_7segment_2_y, bcd_to_7segment_2_z, n6bin_to_bcd_1_s, n6bin_to_bcd_1_t, n6bin_to_bcd_1_u,
       n6bin_to_bcd_1_v, n6bin_to_bcd_1_w, n6bin_to_bcd_1_x, n6bin_to_bcd_1_y, n6bin_to_bcd_1_z;

  _6bin_to_bcd u_6bin_to_bcd_1 (
    .A(in_1), .B(in_2), .C(in_3), .D(in_4), .E(in_5), .F(in_6), .x(n6bin_to_bcd_1_x), .y(n6bin_to_bcd_1_y),
    .z(n6bin_to_bcd_1_z), .u(n6bin_to_bcd_1_u), .v(n6bin_to_bcd_1_v), .w(n6bin_to_bcd_1_w),
    .s(n6bin_to_bcd_1_s), .t(n6bin_to_bcd_1_t));
  bcd_to_7segment bcd_to_7segment_1 (
    .a(n6bin_to_bcd_1_x), .b(n6bin_to_bcd_1_y), .c(n6bin_to_bcd_1_z), .d(n6bin_to_bcd_1_u),
    .x(bcd_to_7segment_1_x), .y(bcd_to_7segment_1_y), .z(bcd_to_7segment_1_z), .u(bcd_to_7segment_1_u),
    .v(bcd_to_7segment_1_v), .w(bcd_to_7segment_1_w), .s(bcd_to_7segment_1_s));
  bcd_to_7segment bcd_to_7segment_2 (
    .a(n6bin_to_bcd_1_v), .b(n6bin_to_bcd_1_w), .c(n6bin_to_bcd_1_s), .d(n6bin_to_bcd_1_t),
    .x(bcd_to_7segment_2_x), .y(bcd_to_7segment_2_y), .z(bcd_to_7segment_2_z), .u(bcd_to_7segment_2_u),
    .v(bcd_to_7segment_2_v), .w(bcd_to_7segment_2_w), .s(bcd_to_7segment_2_s));
  _7_Segment_Display u_7_segment_display_1 (
    .g(bcd_to_7segment_1_s), .f(bcd_to_7segment_1_w), .a(bcd_to_7segment_1_x), .b(bcd_to_7segment_1_y),
    .e(bcd_to_7segment_1_v), .d(bcd_to_7segment_1_u), .c(bcd_to_7segment_1_z));  // open: dp
  _7_Segment_Display u_7_segment_display_2 (
    .g(bcd_to_7segment_2_s), .f(bcd_to_7segment_2_w), .a(bcd_to_7segment_2_x), .b(bcd_to_7segment_2_y),
    .e(bcd_to_7segment_2_v), .d(bcd_to_7segment_2_u), .c(bcd_to_7segment_2_z));  // open: dp
endmodule
