// Logisim project ddsmini.circ as structural Verilog
module main (
  input  Rain,
  input  Wet_Soil,
  input  in_3
);

  wire and_1_out, clock_1_out, comparator_1_eq, comparator_1_lt, nor_1_out, or_1_out;
  wire [5:0] adder_1_out, multiplexer_1_out, Quota_q, Usage_q;

  Clock clock_1 (.out(clock_1_out));
  Register #(.width(6)) Quota (.D(6'b010100), .Q(Quota_q), .clk(clock_1_out));  // open: en, clr
  Register #(.width(6)) Usage (.D(adder_1_out), .en(and_1_out), .Q(Usage_q), .clk(clock_1_out));  // open: clr
  nor nor_1 (nor_1_out, Wet_Soil, Rain);
  Multiplexer #(.width(6)) multiplexer_1 (
    .in0(6'b000001), .in1(6'b000010), .out(multiplexer_1_out), .sel(in_3));  // open: en
  Adder #(.width(6)) adder_1 (.a(Usage_q), .b(multiplexer_1_out), .out(adder_1_out));  // open: cin, cout
  Comparator #(.width(6)) comparator_1 (
    .a(adder_1_out), .b(Quota_q), .eq(comparator_1_eq), .lt(comparator_1_lt));  // open: gt
  or or_1 (or_1_out, comparator_1_eq, comparator_1_lt);
  and and_1 (and_1_out, or_1_out, nor_1_out);
  Hex_Digit_Display hex_digit_display_1 (.value(Usage_q[3:0]));  // open: dp
endmodule
